// Logisim project task1.circ as structural Verilog: 8 circuits, main circuit main
module main (
  input  Clear
);

  wire alu_2_zero_bit, alucontrol_1_alusrc, alucontrol_1_branch, alucontrol_1_jal, alucontrol_1_jr,
       alucontrol_1_jump, alucontrol_1_memtoreg, alucontrol_1_memwrite, alucontrol_1_regwrite, and_1_out,
       clk, not_1_out, or_1_out;
  wire [1:0] alucontrol_1_regdst;
  wire [2:0] alucontrol_1_alu_control;
  wire [4:0] multiplexer_4_out, reg_splitter_1__11_15, reg_splitter_1__16_20, reg_splitter_1__21_25;
  wire [5:0] reg_splitter_1__0_5, reg_splitter_1__26_31;
  wire [15:0] reg_splitter_1__0_15;
  wire [25:0] reg_splitter_1__0_25;
  wire [31:0] adder_1_out, alu_1_alu_output, alu_2_alu_output, bit_extender_1_out, multiplexer_1_out,
       multiplexer_2_out, multiplexer_3_out, multiplexer_5_out, multiplexer_6_out, multiplexer_7_out,
       ram_1_data, ram_2_data, regfile_1_value_0, regfile_1_value_1, register_1_q, shifter_1_out,
       shifter_2_out;

  Multiplexer #(.width(32), .enable("false")) multiplexer_1 (
    .in0(alu_1_alu_output), .in1(adder_1_out), .out(multiplexer_1_out), .sel(and_1_out));
  Multiplexer #(.width(32), .enable("false")) multiplexer_2 (
    .in0(multiplexer_1_out), .in1({alu_1_alu_output[31:28], reg_splitter_1__0_25, 2'b00}),
    .out(multiplexer_2_out), .sel(or_1_out));
  Multiplexer #(.width(32), .enable("false")) multiplexer_3 (
    .in0(multiplexer_2_out), .in1(regfile_1_value_0), .out(multiplexer_3_out), .sel(alucontrol_1_jr));
  Register #(.width(32)) register_1 (.D(multiplexer_3_out), .en(1'b1), .Q(register_1_q), .clk(clk), .clr(Clear));
  ALU alu_1 (.A(32'h4), .B(register_1_q), .S0S1S2(3'b010), .Alu_Output(alu_1_alu_output));  // open: Zero_Bit
  Shifter #(.width(32), .shift("lr")) shifter_1 (.in(register_1_q), .\dist (5'b00010), .out(shifter_1_out));
  ALUControl alucontrol_1 (
    .in_1(reg_splitter_1__26_31), .Funct(reg_splitter_1__0_5), .JR(alucontrol_1_jr),
    .REGWRITE(alucontrol_1_regwrite), .REGDST(alucontrol_1_regdst), .ALUSRC(alucontrol_1_alusrc),
    .BRANCH(alucontrol_1_branch), .MEMWRITE(alucontrol_1_memwrite), .MEMTOREG(alucontrol_1_memtoreg),
    .ALU_Control(alucontrol_1_alu_control), .JUMP(alucontrol_1_jump), .JAL(alucontrol_1_jal));
  or or_1 (or_1_out, alucontrol_1_jump, alucontrol_1_jal);
  and and_1 (and_1_out, alu_2_zero_bit, alucontrol_1_branch);
  Reg_Splitter reg_splitter_1 (
    .in_1(ram_1_data), ._0_5(reg_splitter_1__0_5), ._26_31(reg_splitter_1__26_31),
    ._0_25(reg_splitter_1__0_25), ._21_25(reg_splitter_1__21_25), ._16_20(reg_splitter_1__16_20),
    ._11_15(reg_splitter_1__11_15), ._0_15(reg_splitter_1__0_15));
  RAM #(.addrWidth(24), .dataWidth(32)) ram_1 (
    .addr(shifter_1_out[23:0]), .data(ram_1_data), .sel(1'b1), .clk(clk), .ld(1'b1), .clr(1'b0));
  Multiplexer #(.select(2), .width(5), .enable("false")) multiplexer_4 (
    .in0(reg_splitter_1__16_20), .in1(reg_splitter_1__11_15), .in2({5{1'b1}}), .out(multiplexer_4_out),
    .sel(alucontrol_1_regdst));  // open: in3
  assign bit_extender_1_out = {{16{reg_splitter_1__0_15[15]}}, reg_splitter_1__0_15};  // Bit_Extender bit_extender_1
  Multiplexer #(.width(32), .enable("false")) multiplexer_5 (
    .in0(multiplexer_7_out), .in1(alu_1_alu_output), .out(multiplexer_5_out), .sel(alucontrol_1_jal));
  RegFile regfile_1 (
    .Read_0(reg_splitter_1__21_25), .Read_1(reg_splitter_1__16_20), .RegWrite(alucontrol_1_regwrite),
    .clear(Clear), .write_value(multiplexer_5_out), .write_addr(multiplexer_4_out), .clock(clk),
    .Value_0(regfile_1_value_0), .Value_1(regfile_1_value_1));  // open: v0
  Multiplexer #(.width(32), .enable("false")) multiplexer_6 (
    .in0(regfile_1_value_1), .in1(bit_extender_1_out), .out(multiplexer_6_out), .sel(alucontrol_1_alusrc));
  Shifter #(.width(32)) shifter_2 (.in(bit_extender_1_out), .\dist (5'b00010), .out(shifter_2_out));
  ALU alu_2 (
    .A(regfile_1_value_0), .B(multiplexer_6_out), .S0S1S2(alucontrol_1_alu_control),
    .Zero_Bit(alu_2_zero_bit), .Alu_Output(alu_2_alu_output));
  not not_1 (not_1_out, alucontrol_1_memwrite);
  Adder #(.width(32)) adder_1 (.a(shifter_2_out), .b(alu_1_alu_output), .out(adder_1_out));  // open: cin, cout
  RAM #(.addrWidth(24), .dataWidth(32), .bus("separate")) ram_2 (
    .addr(alu_2_alu_output[23:0]), .din(regfile_1_value_1), .data(ram_2_data), .str(alucontrol_1_memwrite),
    .sel(1'b1), .clk(clk), .ld(not_1_out), .clr(1'b0));
  Clock clock_1 (.out(clk));
  Multiplexer #(.width(32), .enable("false")) multiplexer_7 (
    .in0(alu_2_alu_output), .in1(ram_2_data), .out(multiplexer_7_out), .sel(alucontrol_1_memtoreg));

  // Notes on the sheet:
  //   RedDst
  //   RegWrite
  //   ALUSrc
  //   MemWrite
endmodule

module ALU (
  input  [31:0] A,
  input  [2:0] S0S1S2,
  input  [31:0] B,
  output Zero_Bit,
  output [31:0] Alu_Output
);

  wire comparator_1_lt;
  wire [31:0] adder_1_out, and_1_out, bit_extender_1_out, or_1_out, subtractor_1_out;

  Adder #(.width(32)) adder_1 (.a(B), .b(A), .out(adder_1_out));  // open: cin, cout
  Subtractor #(.width(32)) subtractor_1 (.a(A), .b(B), .out(subtractor_1_out));  // open: bin, bout
  Comparator #(.width(32), .mode("unsigned")) comparator_1 (.a(A), .b(B), .lt(comparator_1_lt));  // open: gt, eq
  assign or_1_out = A | B;  // OR_Gate or_1, 32 bits wide
  assign and_1_out = B & A;  // AND_Gate and_1, 32 bits wide
  assign bit_extender_1_out = {{31{1'b0}}, comparator_1_lt};  // Bit_Extender bit_extender_1
  Multiplexer #(.select(3), .width(32)) multiplexer_1 (
    .in0(and_1_out), .in1(or_1_out), .in2(adder_1_out), .in6(subtractor_1_out), .in7(bit_extender_1_out),
    .out(Alu_Output), .sel(S0S1S2));  // open: in3, in4, in5, en
  Comparator #(.width(32)) comparator_2 (.a({32{1'b0}}), .b(Alu_Output), .eq(Zero_Bit));  // open: gt, lt

  // Notes on the sheet:
  //   Inputs
  //   Output
endmodule

module RegFile (
  input  [4:0] Read_0,
  input  [4:0] Read_1,
  input  RegWrite,
  input  clear,
  input  [31:0] write_value,
  input  [4:0] write_addr,
  input  clock,
  output [31:0] v0,
  output [31:0] Value_0,
  output [31:0] Value_1
);

  wire decoder_1_out1, decoder_1_out2, decoder_1_out3, decoder_1_out4, decoder_1_out5, decoder_1_out6,
       decoder_1_out7, decoder_1_out8, decoder_1_out9, decoder_1_out10, decoder_1_out11, decoder_1_out12,
       decoder_1_out13, decoder_1_out14, decoder_1_out15, decoder_1_out16, decoder_1_out17, decoder_1_out18,
       decoder_1_out19, decoder_1_out20, decoder_1_out21, decoder_1_out22, decoder_1_out23, decoder_1_out24,
       decoder_1_out25, decoder_1_out26, decoder_1_out27, decoder_1_out28, decoder_1_out29, decoder_1_out30,
       decoder_1_out31;
  wire [31:0] a0_q, a1_q, a2_q, a3_q, at_q, fp_q, gp_q, k0_q, k1_q, ra_q, s0_q, s1_q, s2_q, s3_q, s4_q, s5_q,
       s6_q, s7_q, sp_q, t0_q, t1_q, t2_q, t3_q, t4_q, t5_q, t6_q, t7_q, t8_q, t9_q, v1_q;

  Decoder #(.select(5), .disabled(0)) decoder_1 (
    .out1(decoder_1_out1), .out2(decoder_1_out2), .out3(decoder_1_out3), .out4(decoder_1_out4),
    .out5(decoder_1_out5), .out6(decoder_1_out6), .out7(decoder_1_out7), .out8(decoder_1_out8),
    .out9(decoder_1_out9), .out10(decoder_1_out10), .out11(decoder_1_out11), .out12(decoder_1_out12),
    .out13(decoder_1_out13), .out14(decoder_1_out14), .out15(decoder_1_out15), .out16(decoder_1_out16),
    .out17(decoder_1_out17), .out18(decoder_1_out18), .out19(decoder_1_out19), .out20(decoder_1_out20),
    .out21(decoder_1_out21), .out22(decoder_1_out22), .out23(decoder_1_out23), .out24(decoder_1_out24),
    .out25(decoder_1_out25), .out26(decoder_1_out26), .out27(decoder_1_out27), .out28(decoder_1_out28),
    .out29(decoder_1_out29), .out30(decoder_1_out30), .out31(decoder_1_out31), .sel(write_addr), .en(RegWrite));  // open: out0
  Register #(.width(32)) at (.D(write_value), .en(decoder_1_out1), .Q(at_q), .clk(clock), .clr(clear));
  Register #(.width(32)) u_v0 (.D(write_value), .en(decoder_1_out2), .Q(v0), .clk(clock), .clr(clear));
  Register #(.width(32)) v1 (.D(write_value), .en(decoder_1_out3), .Q(v1_q), .clk(clock), .clr(clear));
  Register #(.width(32)) a0 (.D(write_value), .en(decoder_1_out4), .Q(a0_q), .clk(clock), .clr(clear));
  Register #(.width(32)) a1 (.D(write_value), .en(decoder_1_out5), .Q(a1_q), .clk(clock), .clr(clear));
  Register #(.width(32)) a2 (.D(write_value), .en(decoder_1_out6), .Q(a2_q), .clk(clock), .clr(clear));
  Register #(.width(32)) a3 (.D(write_value), .en(decoder_1_out7), .Q(a3_q), .clk(clock), .clr(clear));
  Register #(.width(32)) t0 (.D(write_value), .en(decoder_1_out8), .Q(t0_q), .clk(clock), .clr(clear));
  Register #(.width(32)) t1 (.D(write_value), .en(decoder_1_out9), .Q(t1_q), .clk(clock), .clr(clear));
  Register #(.width(32)) t2 (.D(write_value), .en(decoder_1_out10), .Q(t2_q), .clk(clock), .clr(clear));
  Register #(.width(32)) t3 (.D(write_value), .en(decoder_1_out11), .Q(t3_q), .clk(clock), .clr(clear));
  Register #(.width(32)) t4 (.D(write_value), .en(decoder_1_out12), .Q(t4_q), .clk(clock), .clr(clear));
  Register #(.width(32)) t5 (.D(write_value), .en(decoder_1_out13), .Q(t5_q), .clk(clock), .clr(clear));
  Register #(.width(32)) t6 (.D(write_value), .en(decoder_1_out14), .Q(t6_q), .clk(clock), .clr(clear));
  Register #(.width(32)) t7 (.D(write_value), .en(decoder_1_out15), .Q(t7_q), .clk(clock), .clr(clear));
  Register #(.width(32)) s0 (.D(write_value), .en(decoder_1_out16), .Q(s0_q), .clk(clock), .clr(clear));
  Register #(.width(32)) s1 (.D(write_value), .en(decoder_1_out17), .Q(s1_q), .clk(clock), .clr(clear));
  Register #(.width(32)) s2 (.D(write_value), .en(decoder_1_out18), .Q(s2_q), .clk(clock), .clr(clear));
  Register #(.width(32)) s3 (.D(write_value), .en(decoder_1_out19), .Q(s3_q), .clk(clock), .clr(clear));
  Register #(.width(32)) s4 (.D(write_value), .en(decoder_1_out20), .Q(s4_q), .clk(clock), .clr(clear));
  Register #(.width(32)) s5 (.D(write_value), .en(decoder_1_out21), .Q(s5_q), .clk(clock), .clr(clear));
  Register #(.width(32)) s6 (.D(write_value), .en(decoder_1_out22), .Q(s6_q), .clk(clock), .clr(clear));
  Register #(.width(32)) s7 (.D(write_value), .en(decoder_1_out23), .Q(s7_q), .clk(clock), .clr(clear));
  Register #(.width(32)) t8 (.D(write_value), .en(decoder_1_out24), .Q(t8_q), .clk(clock), .clr(clear));
  Register #(.width(32)) t9 (.D(write_value), .en(decoder_1_out25), .Q(t9_q), .clk(clock), .clr(clear));
  Register #(.width(32)) k0 (.D(write_value), .en(decoder_1_out26), .Q(k0_q), .clk(clock), .clr(clear));
  Register #(.width(32)) k1 (.D(write_value), .en(decoder_1_out27), .Q(k1_q), .clk(clock), .clr(clear));
  Register #(.width(32)) gp (.D(write_value), .en(decoder_1_out28), .Q(gp_q), .clk(clock), .clr(clear));
  Register #(.width(32)) sp (.D(write_value), .en(decoder_1_out29), .Q(sp_q), .clk(clock), .clr(clear));
  Register #(.width(32)) fp (.D(write_value), .en(decoder_1_out30), .Q(fp_q), .clk(clock), .clr(clear));
  Register #(.width(32)) ra (.D(write_value), .en(decoder_1_out31), .Q(ra_q), .clk(clock), .clr(clear));
  Multiplexer #(.select(5), .width(32)) multiplexer_1 (
    .in0({32{1'b0}}), .in1(at_q), .in2(v0), .in3(v1_q), .in4(a0_q), .in5(a1_q), .in6(a2_q), .in7(a3_q),
    .in8(t0_q), .in9(t1_q), .in10(t2_q), .in11(t3_q), .in12(t4_q), .in13(t5_q), .in14(t6_q), .in15(t7_q),
    .in16(s0_q), .in17(s1_q), .in18(s2_q), .in19(s3_q), .in20(s4_q), .in21(s5_q), .in22(s6_q), .in23(s7_q),
    .in24(t8_q), .in25(t9_q), .in26(k0_q), .in27(k1_q), .in28(gp_q), .in29(sp_q), .in30(fp_q), .in31(ra_q),
    .out(Value_0), .sel(Read_0));  // open: en
  Multiplexer #(.select(5), .width(32)) multiplexer_2 (
    .in0({32{1'b0}}), .in1(at_q), .in2(v0), .in3(v1_q), .in4(a0_q), .in5(a1_q), .in6(a2_q), .in7(a3_q),
    .in8(t0_q), .in9(t1_q), .in10(t2_q), .in11(t3_q), .in12(t4_q), .in13(t5_q), .in14(t6_q), .in15(t7_q),
    .in16(s0_q), .in17(s1_q), .in18(s2_q), .in19(s3_q), .in20(s4_q), .in21(s5_q), .in22(s6_q), .in23(s7_q),
    .in24(t8_q), .in25(t9_q), .in26(k0_q), .in27(k1_q), .in28(gp_q), .in29(sp_q), .in30(fp_q), .in31(ra_q),
    .out(Value_1), .sel(Read_1));  // open: en
endmodule

module Reg_Splitter (
  input  [31:0] in_1,
  output [25:0] _0_25,
  output [4:0] _21_25,
  output [4:0] _16_20,
  output [4:0] _11_15,
  output [15:0] _0_15,
  output [5:0] _26_31,
  output [5:0] _0_5
);


  assign _0_5 = in_1[5:0];
  assign _0_15 = in_1[15:0];
  assign _0_25 = in_1[25:0];
  assign _11_15 = in_1[15:11];
  assign _16_20 = in_1[20:16];
  assign _21_25 = in_1[25:21];
  assign _26_31 = in_1[31:26];
endmodule

module ALUControl (
  input  [5:0] in_1,
  input  [5:0] Funct,
  output REGWRITE,
  output [1:0] REGDST,
  output ALUSRC,
  output BRANCH,
  output MEMWRITE,
  output MEMTOREG,
  output [2:0] ALU_Control,
  output JUMP,
  output JAL,
  output JR
);

  wire funt_dec_1_jr;
  wire [1:0] alucntrl_1_aluop;
  wire [2:0] funt_dec_1_ou1;

  ALUCntrl alucntrl_1 (
    .in_1(in_1), .regwrite(REGWRITE), .REGDST(REGDST), .alusrc(ALUSRC), .branch(BRANCH), .memwrite(MEMWRITE),
    .memtoreg(MEMTOREG), .ALUOP(alucntrl_1_aluop), .jump(JUMP), .jal(JAL));
  FUNT_DEC funt_dec_1 (
    .I6(Funct[5]), .I5(Funct[4]), .I4(Funct[3]), .I3(Funct[2]), .I2(Funct[1]), .I1(Funct[0]),
    .OU3(funt_dec_1_ou1[2]), .OU2(funt_dec_1_ou1[1]), .OU1(funt_dec_1_ou1[0]), .JR(funt_dec_1_jr));
  Multiplexer #(.select(2), .width(3), .enable("false")) multiplexer_1 (
    .in0(3'b010), .in1(3'b110), .in2(funt_dec_1_ou1), .out(ALU_Control), .sel(alucntrl_1_aluop));  // open: in3
  and and_1 (JR, ~alucntrl_1_aluop[0], alucntrl_1_aluop[1], funt_dec_1_jr);  // AND_Gate
endmodule

module FUNT_DEC (
  input  I6,
  input  I5,
  input  I4,
  input  I3,
  input  I2,
  input  I1,
  output OU3,
  output OU2,
  output OU1,
  output JR
);

  wire not_1_out, not_3_out, not_4_out, not_5_out, not_6_out, not_7_out;

  not not_1 (not_1_out, I6);
  not not_2 (OU2, I3);
  or or_1 (OU1, I1, I4);
  not not_3 (not_3_out, I6);
  not not_4 (not_4_out, I5);
  not not_5 (not_5_out, I3);
  not not_6 (not_6_out, I2);
  not not_7 (not_7_out, I1);
  or or_2 (OU3, not_1_out, I2);
  and and_1 (JR, not_3_out, not_4_out, I4, not_5_out, not_6_out, not_7_out);
endmodule

module Q2 (
  input  Clear
);

  wire alu_2_zero_bit, alucontrol_1_alusrc, alucontrol_1_branch, alucontrol_1_jal, alucontrol_1_jr,
       alucontrol_1_jump, alucontrol_1_memtoreg, alucontrol_1_memwrite, alucontrol_1_regwrite, and_1_out,
       clk, not_1_out, or_1_out;
  wire [1:0] alucontrol_1_regdst;
  wire [2:0] alucontrol_1_alu_control;
  wire [4:0] multiplexer_4_out, reg_splitter_1__11_15, reg_splitter_1__16_20, reg_splitter_1__21_25;
  wire [5:0] reg_splitter_1__0_5, reg_splitter_1__26_31;
  wire [15:0] reg_splitter_1__0_15;
  wire [27:0] alu_1_alu_output;
  wire [31:0] adder_1_out, alu_2_alu_output, bit_extender_1_out, multiplexer_1_out, multiplexer_2_out,
       multiplexer_3_out, multiplexer_5_out, multiplexer_6_out, multiplexer_7_out, ram_1_data, ram_2_data,
       regfile_1_value_0, regfile_1_value_1, register_1_q, shifter_1_out, shifter_2_out;
  wire [31:2] reg_splitter_1__0_25;

  Multiplexer #(.width(32), .enable("false")) multiplexer_1 (
    .in0({reg_splitter_1__0_25[31:28], alu_1_alu_output}), .in1(adder_1_out), .out(multiplexer_1_out),
    .sel(and_1_out));
  Multiplexer #(.width(32), .enable("false")) multiplexer_2 (
    .in0(multiplexer_1_out), .in1({reg_splitter_1__0_25, 2'b00}), .out(multiplexer_2_out), .sel(or_1_out));
  Multiplexer #(.width(32), .enable("false")) multiplexer_3 (
    .in0(multiplexer_2_out), .in1(regfile_1_value_0), .out(multiplexer_3_out), .sel(alucontrol_1_jr));
  Register #(.width(32)) register_1 (.D(multiplexer_3_out), .en(1'b1), .Q(register_1_q), .clk(clk), .clr(Clear));
  ALU alu_1 (
    .A(32'h4), .B(register_1_q), .S0S1S2(3'b010), .Alu_Output({reg_splitter_1__0_25[31:28], alu_1_alu_output}));  // open: Zero_Bit
  ALUControl alucontrol_1 (
    .in_1(reg_splitter_1__26_31), .Funct(reg_splitter_1__0_5), .JR(alucontrol_1_jr),
    .REGWRITE(alucontrol_1_regwrite), .REGDST(alucontrol_1_regdst), .ALUSRC(alucontrol_1_alusrc),
    .BRANCH(alucontrol_1_branch), .MEMWRITE(alucontrol_1_memwrite), .MEMTOREG(alucontrol_1_memtoreg),
    .ALU_Control(alucontrol_1_alu_control), .JUMP(alucontrol_1_jump), .JAL(alucontrol_1_jal));
  Shifter #(.width(32), .shift("lr")) shifter_1 (.in(register_1_q), .\dist (5'b00010), .out(shifter_1_out));
  and and_1 (and_1_out, alu_2_zero_bit, alucontrol_1_branch);
  or or_1 (or_1_out, alucontrol_1_jump, alucontrol_1_jal);
  RAM #(.addrWidth(24), .dataWidth(32)) ram_1 (
    .addr(shifter_1_out[23:0]), .data(ram_1_data), .sel(1'b1), .clk(clk), .ld(1'b1), .clr(1'b0));
  Reg_Splitter reg_splitter_1 (
    .in_1(ram_1_data), ._0_5(reg_splitter_1__0_5), ._26_31(reg_splitter_1__26_31),
    ._0_25(reg_splitter_1__0_25[27:2]), ._21_25(reg_splitter_1__21_25), ._16_20(reg_splitter_1__16_20),
    ._11_15(reg_splitter_1__11_15), ._0_15(reg_splitter_1__0_15));
  Multiplexer #(.select(2), .width(5), .enable("false")) multiplexer_4 (
    .in0(reg_splitter_1__16_20), .in1(reg_splitter_1__11_15), .in2({5{1'b1}}), .out(multiplexer_4_out),
    .sel(alucontrol_1_regdst));  // open: in3
  assign bit_extender_1_out = {{16{reg_splitter_1__0_15[15]}}, reg_splitter_1__0_15};  // Bit_Extender bit_extender_1
  Multiplexer #(.width(32), .enable("false")) multiplexer_5 (
    .in0(multiplexer_7_out), .in1({reg_splitter_1__0_25[31:28], alu_1_alu_output}), .out(multiplexer_5_out),
    .sel(alucontrol_1_jal));
  RegFile regfile_1 (
    .Read_0(reg_splitter_1__21_25), .Read_1(reg_splitter_1__16_20), .RegWrite(alucontrol_1_regwrite),
    .clear(Clear), .write_value(multiplexer_5_out), .write_addr(multiplexer_4_out), .clock(clk),
    .Value_0(regfile_1_value_0), .Value_1(regfile_1_value_1));  // open: v0
  Multiplexer #(.width(32), .enable("false")) multiplexer_6 (
    .in0(regfile_1_value_1), .in1(bit_extender_1_out), .out(multiplexer_6_out), .sel(alucontrol_1_alusrc));
  Shifter #(.width(32)) shifter_2 (.in(bit_extender_1_out), .\dist (5'b00010), .out(shifter_2_out));
  ALU alu_2 (
    .A(regfile_1_value_0), .B(multiplexer_6_out), .S0S1S2(alucontrol_1_alu_control),
    .Zero_Bit(alu_2_zero_bit), .Alu_Output(alu_2_alu_output));
  not not_1 (not_1_out, alucontrol_1_memwrite);
  Adder #(.width(32)) adder_1 (
    .a(shifter_2_out), .b({reg_splitter_1__0_25[31:28], alu_1_alu_output}), .out(adder_1_out));  // open: cin, cout
  RAM #(.addrWidth(24), .dataWidth(32), .bus("separate")) ram_2 (
    .addr(alu_2_alu_output[23:0]), .din(regfile_1_value_1), .data(ram_2_data), .str(alucontrol_1_memwrite),
    .sel(1'b1), .clk(clk), .ld(not_1_out), .clr(1'b0));
  Clock clock_1 (.out(clk));
  Multiplexer #(.width(32), .enable("false")) multiplexer_7 (
    .in0(alu_2_alu_output), .in1(ram_2_data), .out(multiplexer_7_out), .sel(alucontrol_1_memtoreg));

  // Notes on the sheet:
  //   RedDst
  //   RegWrite
  //   ALUSrc
  //   MemWrite
endmodule

module ALUCntrl (
  input  [5:0] in_1,
  output regwrite,
  output [1:0] REGDST,
  output alusrc,
  output branch,
  output memwrite,
  output memtoreg,
  output [1:0] ALUOP,
  output jump,
  output jal
);

  wire and_2_out, and_3_out, and_5_out, and_6_out, and_7_out, and_8_out, and_9_out, and_10_out, not_1_out,
       not_2_out, not_3_out, not_4_out, not_5_out, not_6_out, not_7_out, not_8_out, not_9_out, not_10_out,
       not_11_out, not_12_out, not_13_out, not_14_out, not_15_out, not_16_out, not_17_out, not_18_out,
       not_19_out, not_20_out, not_21_out, not_22_out, not_23_out, not_24_out, not_25_out, not_26_out;

  not not_1 (not_1_out, in_1[2]);
  not not_2 (not_2_out, in_1[1]);
  not not_3 (not_3_out, in_1[3]);
  not not_4 (not_4_out, in_1[5]);
  not not_5 (not_5_out, in_1[5]);
  not not_6 (not_6_out, in_1[4]);
  not not_7 (not_7_out, in_1[3]);
  not not_8 (not_8_out, in_1[2]);
  not not_9 (not_9_out, in_1[0]);
  not not_10 (not_10_out, in_1[3]);
  not not_11 (not_11_out, in_1[1]);
  or or_1 (alusrc, in_1[1], in_1[3]);
  not not_12 (not_12_out, in_1[5]);
  not not_13 (not_13_out, in_1[4]);
  not not_14 (not_14_out, in_1[3]);
  and and_1 (memwrite, in_1[5], in_1[3]);
  not not_15 (not_15_out, in_1[5]);
  not not_16 (not_16_out, in_1[4]);
  not not_17 (not_17_out, in_1[3]);
  not not_18 (not_18_out, in_1[2]);
  not not_19 (not_19_out, in_1[3]);
  not not_20 (not_20_out, in_1[2]);
  not not_21 (not_21_out, in_1[1]);
  not not_22 (not_22_out, in_1[5]);
  not not_23 (not_23_out, in_1[4]);
  not not_24 (not_24_out, in_1[3]);
  not not_25 (not_25_out, in_1[5]);
  not not_26 (not_26_out, in_1[5]);
  and and_2 (and_2_out, not_1_out, not_2_out);
  and and_3 (and_3_out, not_3_out, in_1[0]);
  and and_4 (REGDST[1], not_4_out, in_1[1]);
  and and_5 (and_5_out, not_5_out, not_6_out, not_7_out, not_8_out, not_9_out);
  and and_6 (and_6_out, not_10_out, not_11_out);
  and and_7 (and_7_out, not_12_out, not_13_out, not_14_out, in_1[1]);
  and and_8 (and_8_out, not_15_out, not_16_out, not_17_out, not_18_out);
  and and_9 (and_9_out, not_19_out, not_20_out, not_21_out);
  and and_10 (and_10_out, not_22_out, not_23_out, not_24_out, in_1[1]);
  and and_11 (jump, not_25_out, in_1[1]);
  and and_12 (jal, not_26_out, in_1[0]);
  or or_2 (regwrite, and_2_out, and_3_out);
  or or_3 (REGDST[0], and_5_out, and_6_out);
  or or_4 (branch, and_7_out, in_1[2]);
  or or_5 (ALUOP[1], and_8_out, and_9_out);
  or or_6 (ALUOP[0], and_10_out, in_1[2]);

  assign memtoreg = in_1[1];
endmodule
